// Logisim project pipelined_riscv_cpu.circ as structural Verilog: 1 circuit, main circuit main
module main (
  input  RST
);

  wire [0:0] adder_1_cout;
  wire [31:0] ID_EX_Imm_q, IF_ID_Instr_q, PC_q;

  Clock CLK ();  // open: out
  Register #(.width(32)) PC (.Q(PC_q));  // open: D, en, clk, clr
  Adder #(.width(32)) adder_1 (.cout(adder_1_cout[0]));  // open: a, b, out, cin
  ROM #(.addrWidth(8), .dataWidth(32)) Instr_Mem ();  // open: addr, data
  // Register #(.width(32)) IF_ID_PC: pin names not known; wires that end beside it: PC_q
  Register #(.width(32)) IF_ID_Instr (.Q(IF_ID_Instr_q));  // open: D, en, clk, clr
  // RAM #(.addrWidth(5), .dataWidth(32)) RegFile: pin names not known; wires that end beside it: IF_ID_Instr_q
  Register #(.width(32)) ID_EX_RS1 ();  // open: D, en, clk, Q, clr
  Register #(.width(32)) ID_EX_RS2 (.en(ID_EX_Imm_q[0]));  // open: D, clk, Q, clr
  Register #(.width(32)) ID_EX_Imm (.Q(ID_EX_Imm_q));  // open: D, en, clk, clr
  // Multiplexer #(.width(32)) Fwd_A: pin names not known; wires that end beside it: IF_ID_Instr_q, IF_ID_Instr_q
  Multiplexer #(.width(32)) Fwd_B ();  // open: in0, in1, out, sel
  // Adder #(.width(32)) ALU: pin names not known; wires that end beside it: IF_ID_Instr_q
  Register #(.width(32)) EX_MEM_ALU ();  // open: D, en, clk, Q, clr
  Register #(.width(32)) EX_MEM_Data ();  // open: D, en, Q, clk, clr
  RAM #(.addrWidth(10), .dataWidth(32)) Data_Mem (.data(IF_ID_Instr_q));  // open: addr, sel, clk, ld, clr
  Register #(.width(32)) MEM_WB_Data ();  // open: D, en, clk, Q, clr
  Register #(.width(5)) MEM_WB_RD ();  // open: D, en, Q, clk, clr
  Multiplexer #(.width(32)) WB_Mux (.out(IF_ID_Instr_q));  // open: in0, in1, sel
  // Pins of 1 and 32 bits meet at {31'h2, adder_1_cout[0]}
  // Pins of 1 and 32 bits meet at ID_EX_Imm_q
  // also tied to GND on the sheet: adder_1_cout[0]

  // Notes on the sheet:
  //   IF STAGE
  //   Pipeline Stages:
  //   IF  - Instruction Fetch
  //   ID  - Instruction Decode
  //   EX  - Execute
  //   MEM - Memory Access
  //   WB  - Write Back
  //   IF/ID
  //   Load-Use stalls
  //   Branch flush
  //   Decode
  //   Logic
  //   HAZARD UNIT
  //   5-Stage Pipelined RISC-V CPU
  //   ID STAGE
  //   Control Signals: MemRead, MemWrite, RegWrite, ALUOp, Branch
  //   Features:
  //   • Data Forwarding (EX-EX, MEM-EX)
  //   • Hazard Detection (Load-Use)
  //   • Branch Prediction (Flush on taken)
  //   • RV32I Base Instruction Set
  //   ID/EX
  //   Detects RAW hazards
  //   Controls Fwd_A/Fwd_B muxes
  //   EX STAGE
  //   FORWARDING UNIT
  //   Forwarding Paths:
  //   EX/MEM → EX (bypass recent ALU)
  //   MEM/WB → EX (bypass older result)
  //   MEM/WB → ID (writeback to regfile)
  //   Branch
  //   Logic
  //   EX/MEM
  //   MEM STAGE
  //   MEM/WB
  //   WB STAGE
endmodule
